// Logisim project s-mips.circ as structural Verilog: 9 circuits, main circuit S-MIPS Board
module S_MIPS_Board (
  input  DESHABILITAR_DISPATCHER,
  output halt
);

  wire button_1_out, CLK, CS, d_ff_1_q, LCLR, LoadRAM, LoadRAMOn, LW, R_R_W, R_W, ram_dispatcher_1_finished,
       RCS, Reset_out, RST, TTY_EN;
  wire [2:0] KDB;
  wire [3:0] LMask, Mask, ram_1_read_time, ram_1_write_time, RMask;
  wire [6:0] KDB_DATA, TTY_DATA;
  wire [15:0] Addr, LAddr, RAddr;
  wire [31:0] I0, I1, I2, I3, LData, ram_1_data_out_0, ram_1_data_out_1, ram_1_data_out_2, ram_1_data_out_3,
       RI0, RI1, RI2, RI3;

  TTY #(.rows(25), .cols(80)) tty_1 (.data(TTY_DATA), .clk(CLK), .we(TTY_EN), .clr(RST));
  not not_1 (LoadRAMOn, ram_dispatcher_1_finished);
  RAM_Dispatcher ram_dispatcher_1 (
    .WriteTime(ram_1_write_time), .Clock(CLK), .Data(LData), .Address(LAddr), .Mask(LMask),
    .Finished(ram_dispatcher_1_finished), .Write(LW), .CLR(LCLR));
  Keyboard #(.buflen(64)) keyboard_1 (.clk(CLK), .re(KDB[0]), .avail(KDB[2]), .data(KDB_DATA));  // open: clr
  RAM ram_1 (
    .Address(RAddr), .Data_Out_0(ram_1_data_out_0), .Data_Out_1(ram_1_data_out_1),
    .Data_Out_2(ram_1_data_out_2), .Data_Out_3(ram_1_data_out_3), .Data_In_0(RI0), .Data_In_1(RI1),
    .Data_In_2(RI2), .Data_In_3(RI3), .Mask(RMask), .nRead_Write(R_R_W), .Chip_Select(RCS),
    .Read_Time(ram_1_read_time), .Reset(button_1_out), .Write_Time(ram_1_write_time));
  Button button_1 (.out(button_1_out));
  D_Flip_Flop d_ff_1 (.clk(CLK), .D(1'b1), .Q(d_ff_1_q), .reset(Reset_out));  // open: Qn, preset, en
  Button Reset (.out(Reset_out));
  S_MIPS s_mips_1 (
    .Kbd_Enable(KDB[0]), .Address(Addr), .Kbd_Clear(KDB[1]), .Kbd_Available(KDB[2]), .RAM_In_0(I0),
    .Kbd_ASCII_Data(KDB_DATA), .RAM_In_1(I1), .TTY_Enable(TTY_EN), .RAM_In_2(I2), .RAM_In_3(I2),
    .TTY_ASCII_Data(TTY_DATA), .Reset(RST), .RAM_Out_0(ram_1_data_out_0), .Clock(CLK),
    .RAM_Out_1(ram_1_data_out_1), .Stop(halt), .RAM_Out_2(ram_1_data_out_2), .RAM_Out_3(ram_1_data_out_3),
    .Mask(Mask), .Read_Time(ram_1_read_time), .Write_Time(ram_1_write_time), .nRead_Write(R_W),
    .Chip_Select(CS));
  D_Flip_Flop d_ff_2 (.clk(CLK), .D(d_ff_1_q), .Qn(LCLR), .reset(Reset_out));  // open: Q, preset, en
  or or_1 (RST, LCLR, LoadRAM);
  Clock clock_1 (.out(CLK));
  Multiplexer #(.width(32), .enable("false")) multiplexer_1 (.in0(I0), .in1(LData), .out(RI0), .sel(LoadRAM));
  Multiplexer #(.width(32), .enable("false")) multiplexer_2 (.in0(I1), .in1(LData), .out(RI1), .sel(LoadRAM));
  Multiplexer #(.width(32), .enable("false")) multiplexer_3 (.in0(I2), .in1(LData), .out(RI2), .sel(LoadRAM));
  Multiplexer #(.width(32), .enable("false")) multiplexer_4 (.in0(I3), .in1(LData), .out(RI3), .sel(LoadRAM));
  and and_1 (LoadRAM, ~DESHABILITAR_DISPATCHER, LoadRAMOn);  // AND_Gate
  Multiplexer #(.width(16), .enable("false")) multiplexer_5 (.in0(Addr), .in1(LAddr), .out(RAddr), .sel(LoadRAM));
  Multiplexer #(.width(4), .enable("false")) multiplexer_6 (.in0(Mask), .in1(LMask), .out(RMask), .sel(LoadRAM));
  Multiplexer #(.enable("false")) multiplexer_7 (.in0(CS), .in1(LW), .out(RCS), .sel(LoadRAM));
  Multiplexer #(.enable("false")) multiplexer_8 (.in0(R_W), .in1(LW), .out(R_R_W), .sel(LoadRAM));

  // Notes on the sheet:
  //   NO MODIFICAR
  //   Keyboard
endmodule

module RAM (
  input  [15:0] Address,
  input  [31:0] Data_In_0,
  input  [31:0] Data_In_1,
  input  [31:0] Data_In_2,
  input  [31:0] Data_In_3,
  input  [3:0] Mask,
  input  nRead_Write,
  input  Chip_Select,
  input  Reset,
  output [31:0] Data_Out_0,
  output [31:0] Data_Out_1,
  output [31:0] Data_Out_2,
  output [31:0] Data_Out_3,
  output [3:0] Read_Time,
  output [3:0] Write_Time
);

  wire and_2_out, and_3_out, and_4_out, and_5_out, and_6_out, and_7_out, and_8_out, and_9_out, Changed, CLK,
       comparator_2_eq, comparator_3_eq, comparator_4_eq, comparator_5_eq, comparator_6_eq, Count,
       demultiplexer_3_out0, Idle, Idle_q, Load, Load0, Load1, nand_1_out, or_1_out, or_2_out, or_3_out,
       or_4_out, or_5_out, or_6_out, or_7_out, or_8_out, or_9_out, or_10_out, Proc_q, Update_Mem, Zero_Time;
  wire [3:0] counter_1_q, multiplexer_1_out, subtractor_1_out;
  wire [31:0] register_1_q, register_2_q, register_3_q, register_4_q, register_5_q;

  // Probe on 4'b0011
  // Probe on 4'b0010
  Multiplexer #(.width(4), .enable("false")) multiplexer_1 (
    .in0(4'b0011), .in1(4'b0010), .out(multiplexer_1_out), .sel(nRead_Write));
  or or_1 (or_1_out, Idle, Update_Mem);
  or or_2 (or_2_out, ~Chip_Select, Reset);  // OR_Gate
  Subtractor #(.width(4)) subtractor_1 (.a(multiplexer_1_out), .b(4'b0010), .out(subtractor_1_out));  // open: bin, bout
  Demultiplexer #(.enable("false")) demultiplexer_1 (.out0(Idle), .out1(Load0), .in(Idle_q), .sel(Changed));
  D_Flip_Flop u_Idle (.clk(CLK), .D(or_1_out), .Q(Idle_q), .preset(or_2_out));  // open: Qn, en, reset
  // Probe on counter_1_q
  Counter #(.width(4), .max('hf)) counter_1 (
    .load(Load), .D(subtractor_1_out), .count(Count), .Q(counter_1_q), .clk(CLK), .clr(or_3_out));  // open: carry
  or or_3 (or_3_out, ~Chip_Select, Reset);  // OR_Gate
  Comparator #(.width(4), .mode("unsigned")) comparator_1 (
    .a(4'b0000), .b(counter_1_q), .eq(Zero_Time));  // open: gt, lt
  or or_4 (or_4_out, Count, Load0, Load1);
  Register #(.width(32)) register_1 (.D(Data_In_0), .en(Chip_Select), .Q(register_1_q), .clk(CLK), .clr(or_5_out));
  or or_5 (or_5_out, ~Chip_Select, Reset);  // OR_Gate
  Register #(.width(32)) register_2 (.D(Data_In_1), .en(Chip_Select), .Q(register_2_q), .clk(CLK), .clr(or_6_out));
  or or_6 (or_6_out, ~Chip_Select, Reset);  // OR_Gate
  Register #(.width(32)) register_3 (.D(Data_In_2), .en(Chip_Select), .Q(register_3_q), .clk(CLK), .clr(or_7_out));
  or or_7 (or_7_out, ~Chip_Select, Reset);  // OR_Gate
  Register #(.width(32)) register_4 (.D(Data_In_3), .en(Chip_Select), .Q(register_4_q), .clk(CLK), .clr(or_8_out));
  or or_8 (or_8_out, ~Chip_Select, Reset);  // OR_Gate
  Register #(.width(32)) register_5 (
    .D({{11{1'b1}}, nRead_Write, Mask, Address}), .en(Chip_Select), .Q(register_5_q), .clk(CLK),
    .clr(or_9_out));
  or or_9 (or_9_out, ~Chip_Select, Reset);  // OR_Gate
  D_Flip_Flop Proc (.clk(CLK), .D(or_4_out), .Q(Proc_q), .reset(or_10_out));  // open: Qn, preset, en
  or or_10 (or_10_out, ~Chip_Select, Reset);  // OR_Gate
  Demultiplexer #(.enable("false")) demultiplexer_2 (
    .out0(Count), .out1(Update_Mem), .in(demultiplexer_3_out0), .sel(Zero_Time));
  Demultiplexer #(.enable("false")) demultiplexer_3 (
    .out0(demultiplexer_3_out0), .out1(Load1), .in(Proc_q), .sel(Changed));
  Clock clock_1 (.out(CLK));
  Comparator #(.width(32)) comparator_2 (.a(register_1_q), .b(Data_In_0), .eq(comparator_2_eq));  // open: gt, lt
  Comparator #(.width(32)) comparator_3 (.a(register_2_q), .b(Data_In_1), .eq(comparator_3_eq));  // open: gt, lt
  Comparator #(.width(32)) comparator_4 (.a(register_3_q), .b(Data_In_2), .eq(comparator_4_eq));  // open: gt, lt
  Comparator #(.width(32)) comparator_5 (.a(register_4_q), .b(Data_In_3), .eq(comparator_5_eq));  // open: gt, lt
  Comparator #(.width(32)) comparator_6 (
    .a(register_5_q), .b({{11{1'b1}}, nRead_Write, Mask, Address}), .eq(comparator_6_eq));  // open: gt, lt
  nand nand_1 (nand_1_out, comparator_6_eq, comparator_2_eq, comparator_3_eq, comparator_4_eq, comparator_5_eq);
  and and_1 (Changed, nand_1_out, Chip_Select);
  or or_11 (Load, Count, Load1, Load0);
  and and_2 (and_2_out, Mask[0], Update_Mem, nRead_Write);
  and and_3 (and_3_out, Mask[1], Update_Mem, nRead_Write);
  and and_4 (and_4_out, Mask[2], Update_Mem, nRead_Write);
  and and_5 (and_5_out, Mask[3], Update_Mem, nRead_Write);
  RAM_part #(.addrWidth(16), .dataWidth(32), .bus("separate")) ram_1 (
    .addr(Address), .din(Data_In_0), .data(Data_Out_0), .str(and_2_out), .sel(Chip_Select), .clk(CLK),
    .ld(and_6_out), .clr(Reset));
  and and_6 (and_6_out, ~nRead_Write, Idle);  // AND_Gate
  RAM_part #(.addrWidth(16), .dataWidth(32), .bus("separate")) ram_2 (
    .addr(Address), .din(Data_In_1), .data(Data_Out_1), .str(and_3_out), .sel(Chip_Select), .clk(CLK),
    .ld(and_7_out), .clr(Reset));
  and and_7 (and_7_out, ~nRead_Write, Idle);  // AND_Gate
  RAM_part #(.addrWidth(16), .dataWidth(32), .bus("separate")) ram_3 (
    .addr(Address), .din(Data_In_2), .data(Data_Out_2), .str(and_4_out), .sel(Chip_Select), .clk(CLK),
    .ld(and_8_out), .clr(Reset));
  and and_8 (and_8_out, ~nRead_Write, Idle);  // AND_Gate
  RAM_part #(.addrWidth(16), .dataWidth(32), .bus("separate")) ram_4 (
    .addr(Address), .din(Data_In_3), .data(Data_Out_3), .str(and_5_out), .sel(Chip_Select), .clk(CLK),
    .ld(and_9_out), .clr(Reset));
  and and_9 (and_9_out, ~nRead_Write, Idle);  // AND_Gate

  assign Read_Time = 4'b0011;
  assign Write_Time = 4'b0010;

  // Other names for the same wires on the sheet: M0 = Mask[0]; M1 = Mask[1]; M2 = Mask[2]; M3 = Mask[3];
  //   RW = nRead_Write; CLR = Reset; CS = Chip_Select; Load2 = Count

  // Notes on the sheet:
  //   NO MODIFICAR
  //   excepto quizás los valores RT y WT
  //   BANK0
  //   BANK1
  //   BANK2
  //   BANK3
endmodule

module S_MIPS (
  input  Kbd_Available,
  input  [6:0] Kbd_ASCII_Data,
  input  [31:0] RAM_Out_0,
  input  [31:0] RAM_Out_1,
  input  Reset,
  input  [31:0] RAM_Out_2,
  input  Clock,
  input  [31:0] RAM_Out_3,
  input  [3:0] Read_Time,
  input  [3:0] Write_Time,
  output Kbd_Enable,
  output [15:0] Address,
  output Kbd_Clear,
  output TTY_Enable,
  output [6:0] TTY_ASCII_Data,
  output Stop,
  output [31:0] RAM_In_0,
  output [31:0] RAM_In_1,
  output [31:0] RAM_In_2,
  output [31:0] RAM_In_3,
  output [3:0] Mask,
  output nRead_Write,
  output Chip_Select
);


  // Other names for the same wires on the sheet: CLK = Clock; CLR = Reset; CS = Chip_Select;
  //   KBD_AVAIL = Kbd_Available; KBD_CLR = Kbd_Clear; KBD_DATA[6:0] = Kbd_ASCII_Data; RAM_A[15:0] = Address;
  //   RAM_INPUT_0[31:0] = RAM_In_0; RAM_INPUT_1[31:0] = RAM_In_1; RAM_INPUT_2[31:0] = RAM_In_2;
  //   RAM_INPUT_3[31:0] = RAM_In_3; RAM_MASK[3:0] = Mask; RAM_OUTPUT_0[31:0] = RAM_Out_0;
  //   RAM_OUTPUT_1[31:0] = RAM_Out_1; RAM_OUTPUT_2[31:0] = RAM_Out_2; RAM_OUTPUT_3[31:0] = RAM_Out_3;
  //   RW = nRead_Write; TTY_DATA[6:0] = TTY_ASCII_Data

  // Notes on the sheet:
  //   RAM ADDRESS
  //   DATA FROM RAM
  //   DATA TO RAM
  //   DATA WRITE MASK
  //   RAM TIMING
  //   RAM CONTROL
  //   KEYBOARD
  //   TTY
  //   SEQUENCING
endmodule

module RAM_Dispatcher (
  input  [3:0] WriteTime,
  input  Clock,
  input  CLR,
  output [31:0] Data,
  output [15:0] Address,
  output [3:0] Mask,
  output Finished,
  output Write
);

  wire demultiplexer_2_out1, demultiplexer_3_out1, End, IDLE_q, IncAddr, Load, or_1_out, or_2_out, While_q,
       WriteEnd;
  wire [3:0] counter_1_q;
  wire [31:0] CurrentAddress_q;

  Counter #(.width(32), .max('hffffffff)) CurrentAddress (
    .count(IncAddr), .Q({CurrentAddress_q[31:18], Address, CurrentAddress_q[1:0]}), .clk(Clock), .clr(CLR));  // open: load, D, carry
  or or_1 (or_1_out, IncAddr, demultiplexer_3_out1, Finished);
  D_Flip_Flop IDLE (.clk(Clock), .D(or_1_out), .Q(IDLE_q), .preset(CLR));  // open: Qn, en, reset
  Demultiplexer #(.enable("false")) demultiplexer_1 (.out0(Load), .out1(Finished), .in(IDLE_q), .sel(End));
  D_Flip_Flop While (.clk(Clock), .D(or_2_out), .Q(While_q), .reset(CLR));  // open: Qn, preset, en
  or or_2 (or_2_out, Write, Load);
  RAM_part #(.addrWidth(18), .dataWidth(32)) ram_1 (
    .addr({Address, CurrentAddress_q[1:0]}), .data(Data), .clk(Clock));  // open: sel, ld, clr
  Demultiplexer #(.enable("false")) demultiplexer_2 (
    .out0(Write), .out1(demultiplexer_2_out1), .in(While_q), .sel(WriteEnd));
  Decoder #(.select(2)) decoder_1 (
    .out0(Mask[0]), .out1(Mask[1]), .out2(Mask[2]), .out3(Mask[3]), .sel(CurrentAddress_q[1:0]));  // open: en
  Demultiplexer #(.enable("false")) demultiplexer_3 (
    .out0(IncAddr), .out1(demultiplexer_3_out1), .in(demultiplexer_2_out1), .sel(End));
  Counter #(.width(4), .max('hf)) counter_1 (
    .load(Load), .D(WriteTime), .count(Write), .Q(counter_1_q), .clk(Clock));  // open: carry, clr
  Comparator #(.width(32)) comparator_1 (.a(Data), .b({32{1'b1}}), .eq(End));  // open: gt, lt
  Comparator #(.width(4)) comparator_2 (.a(4'b0000), .b(counter_1_q), .eq(WriteEnd));  // open: gt, lt

  // Other names for the same wires on the sheet: CLK = Clock; Count = Write; WT[3:0] = WriteTime
endmodule

module ALU (
  input  [3:0] in_1,
  input  [31:0] in_2,
  input  [31:0] in_3,
  output [31:0] out_4
);

  wire clock_1_out, comparator_1_lt, comparator_2_lt;
  wire [31:0] add, \and , \nor , \or , rnd, slt, sltu, sub, \xor ;

  assign \and  = in_2 & in_3;  // AND_Gate and_1, 32 bits wide
  assign \or  = in_2 | in_3;  // OR_Gate or_1, 32 bits wide
  assign \nor  = ~(in_2 | in_3);  // NOR_Gate nor_1, 32 bits wide
  assign \xor  = in_2 ^ in_3;  // XOR_Gate xor_1, 32 bits wide
  Comparator #(.width(32)) comparator_1 (.a(in_2), .b(in_3), .lt(comparator_1_lt));  // open: gt, eq
  Comparator #(.width(32), .mode("unsigned")) comparator_2 (.a(in_2), .b(in_3), .lt(comparator_2_lt));  // open: gt, eq
  Clock clock_1 (.out(clock_1_out));
  // Probe on in_2
  // Probe on in_3
  Adder #(.width(32)) adder_1 (.a(in_2), .b(in_3), .out(add));  // open: cin, cout
  Subtractor #(.width(32)) subtractor_1 (.a(in_2), .b(in_3), .out(sub));  // open: bin, bout
  Multiplexer #(.width(32), .enable("false")) multiplexer_1 (
    .in0({32{1'b0}}), .in1(32'h1), .out(slt), .sel(comparator_1_lt));
  Multiplexer #(.width(32), .enable("false")) multiplexer_2 (
    .in0({32{1'b0}}), .in1(32'h1), .out(sltu), .sel(comparator_2_lt));
  Random #(.width(32)) random_1 (.clk(clock_1_out), .out(rnd));  // open: next, clr
  Multiplexer #(.select(4), .width(32), .enable("false")) multiplexer_3 (
    .in0({32{1'b0}}), .in1(add), .in2(sub), .in3(slt), .in4(sltu), .in5(\and ), .in6(\or ), .in7(\nor ),
    .in8(\xor ), .in9(rnd), .out(out_4), .sel(in_1));  // open: in10, in11, in12, in13, in14, in15
  // Probe on out_4

  // Other names for the same wires on the sheet: A[31:0] = in_2; B[31:0] = in_3; op[3:0] = in_1
endmodule

module Divider (
  input  [31:0] in_1,
  input  [31:0] in_2,
  input  in_3,
  output [31:0] out_4,
  output [31:0] out_5
);

  wire a_neg, b_neg, O_neg;
  wire [31:0] adder_1_out, b_t, divider_1_out, multiplexer_3_out, multiplexer_4_out, negator_1_out,
       negator_2_out, negator_3_out, negator_4_out, O, R, subtractor_1_out;

  xor xor_1 (O_neg, a_neg, b_neg);
  Multiplexer #(.width(32)) multiplexer_1 (.in0(in_2), .in1(negator_1_out), .out(b_t), .sel(b_neg));  // open: en
  Negator #(.width(32)) negator_1 (.in(in_2), .out(negator_1_out));
  and and_1 (a_neg, in_1[31], in_3);
  and and_2 (b_neg, in_3, in_2[31]);
  Negator #(.width(32)) negator_2 (.in(in_1), .out(negator_2_out));
  Negator #(.width(32)) negator_3 (.in(in_2), .out(negator_3_out));
  Multiplexer #(.width(32)) multiplexer_2 (.in0(O), .in1(negator_4_out), .out(out_4), .sel(O_neg));  // open: en
  Negator #(.width(32)) negator_4 (.in(O), .out(negator_4_out));
  Multiplexer #(.width(32)) multiplexer_3 (
    .in0(in_1), .in1(negator_2_out), .out(multiplexer_3_out), .sel(a_neg));  // open: en
  Multiplexer #(.width(32)) multiplexer_4 (
    .in0(in_2), .in1(negator_3_out), .out(multiplexer_4_out), .sel(b_neg));  // open: en
  Divider_part #(.width(32)) divider_1 (
    .a(multiplexer_3_out), .b(multiplexer_4_out), .out(divider_1_out), .rem(R));  // open: upper
  Adder #(.width(32)) adder_1 (.a(divider_1_out), .b(32'h1), .out(adder_1_out));  // open: cin, cout
  Multiplexer #(.width(32)) multiplexer_5 (.in0(divider_1_out), .in1(adder_1_out), .out(O), .sel(a_neg));  // open: en
  Multiplexer #(.width(32)) multiplexer_6 (.in0(R), .in1(subtractor_1_out), .out(out_5), .sel(a_neg));  // open: en
  Subtractor #(.width(32)) subtractor_1 (.a(b_t), .b(R), .out(subtractor_1_out));  // open: bin, bout

  // Other names for the same wires on the sheet: a[31:0] = in_1; b[31:0] = in_2; OUTPUT[31:0] = out_4;
  //   REMAINDER[31:0] = out_5; Signo = in_3
endmodule

module Register_File (
  input  in_1,
  input  in_2,
  input  in_3,
  input  [4:0] in_4,
  input  [4:0] in_5,
  input  [31:0] in_6,
  input  in_7,
  input  in_8,
  input  in_9,
  input  [4:0] in_10,
  output [31:0] out_11,
  output [31:0] out_12,
  output [31:0] out_13
);

  wire L0, L1, L2, L3, L4, L5, L6, L7, L8, L9, L10, L11, L12, L13, L14, L15, L16, L17, L18, L19, L20, L21,
       L22, L23, L24, L25, L26, L27, L28, L29, L30, L31, or_1_out, or_2_out;
  wire [31:0] adder_1_out, InputSP, multiplexer_3_out, Out0, Out1, Out2, Out3, Out4, Out5, Out6, Out7, Out8,
       Out9, Out10, Out11, Out12, Out13, Out14, Out15, Out16, Out17, Out18, Out19, Out20, Out21, Out22,
       Out23, Out24, Out25, Out26, Out27, Out28, Out29, Out30, subtractor_1_out;

  Register #(.width(32)) register_1 (.D({32{1'b0}}), .en(L0), .Q(Out0), .clk(in_7), .clr(in_1));
  Register #(.width(32)) register_2 (.D(in_6), .en(L8), .Q(Out8), .clk(in_7), .clr(in_1));
  Register #(.width(32)) register_3 (.D(in_6), .en(L16), .Q(Out16), .clk(in_7), .clr(in_1));
  Register #(.width(32)) register_4 (.D(in_6), .en(L24), .Q(Out24), .clk(in_7), .clr(in_1));
  Demultiplexer #(.select(5)) demultiplexer_1 (
    .out0(L0), .out1(L1), .out2(L2), .out3(L3), .out4(L4), .out5(L5), .out6(L6), .out7(L7), .out8(L8),
    .out9(L9), .out10(L10), .out11(L11), .out12(L12), .out13(L13), .out14(L14), .out15(L15), .out16(L16),
    .out17(L17), .out18(L18), .out19(L19), .out20(L20), .out21(L21), .out22(L22), .out23(L23), .out24(L24),
    .out25(L25), .out26(L26), .out27(L27), .out28(L28), .out29(L29), .out30(L30), .in(in_2), .sel(in_4));  // open: out31, en
  Register #(.width(32)) register_5 (.D(in_6), .en(L1), .Q(Out1), .clk(in_7), .clr(in_1));
  Register #(.width(32)) register_6 (.D(in_6), .en(L9), .Q(Out9), .clk(in_7), .clr(in_1));
  Register #(.width(32)) register_7 (.D(in_6), .en(L17), .Q(Out17), .clk(in_7), .clr(in_1));
  Register #(.width(32)) register_8 (.D(in_6), .en(L25), .Q(Out25), .clk(in_7), .clr(in_1));
  Register #(.width(32)) register_9 (.D(in_6), .en(L2), .Q(Out2), .clk(in_7), .clr(in_1));
  Register #(.width(32)) register_10 (.D(in_6), .en(L10), .Q(Out10), .clk(in_7), .clr(in_1));
  Register #(.width(32)) register_11 (.D(in_6), .en(L18), .Q(Out18), .clk(in_7), .clr(in_1));
  Register #(.width(32)) register_12 (.D(in_6), .en(L26), .Q(Out26), .clk(in_7), .clr(in_1));
  multiplexer multiplexer_1 (
    .in_1(in_5), .in_2(Out0), .in_3(Out1), .in_4(Out2), .in_5(Out3), .in_6(Out4), .in_7(Out5), .in_8(Out6),
    .in_9(Out7), .in_10(Out8), .in_11(Out9), .in_12(Out10), .in_13(Out11), .in_14(Out12), .in_15(Out13),
    .in_16(Out14), .in_17(Out15), .in_18(Out16), .in_19(Out17), .in_20(Out18), .in_21(Out19), .in_22(Out20),
    .in_23(Out21), .in_24(Out22), .in_25(Out23), .in_26(Out24), .in_27(Out25), .in_28(Out26), .in_29(Out27),
    .in_30(Out28), .in_31(Out29), .in_32(Out30), .in_33(out_13), .out_34(out_11));
  Register #(.width(32)) register_13 (.D(in_6), .en(L3), .Q(Out3), .clk(in_7), .clr(in_1));
  Register #(.width(32)) register_14 (.D(in_6), .en(L11), .Q(Out11), .clk(in_7), .clr(in_1));
  Register #(.width(32)) register_15 (.D(in_6), .en(L19), .Q(Out19), .clk(in_7), .clr(in_1));
  Register #(.width(32)) register_16 (.D(in_6), .en(L27), .Q(Out27), .clk(in_7), .clr(in_1));
  Register #(.width(32)) register_17 (.D(in_6), .en(L4), .Q(Out4), .clk(in_7), .clr(in_1));
  Register #(.width(32)) register_18 (.D(in_6), .en(L12), .Q(Out12), .clk(in_7), .clr(in_1));
  Register #(.width(32)) register_19 (.D(in_6), .en(L20), .Q(Out20), .clk(in_7), .clr(in_1));
  Register #(.width(32)) register_20 (.D(in_6), .en(L28), .Q(Out28), .clk(in_7), .clr(in_1));
  multiplexer multiplexer_2 (
    .in_1(in_10), .in_2(Out0), .in_3(Out1), .in_4(Out2), .in_5(Out3), .in_6(Out4), .in_7(Out5), .in_8(Out6),
    .in_9(Out7), .in_10(Out8), .in_11(Out9), .in_12(Out10), .in_13(Out11), .in_14(Out12), .in_15(Out13),
    .in_16(Out14), .in_17(Out15), .in_18(Out16), .in_19(Out17), .in_20(Out18), .in_21(Out19), .in_22(Out20),
    .in_23(Out21), .in_24(Out22), .in_25(Out23), .in_26(Out24), .in_27(Out25), .in_28(Out26), .in_29(Out27),
    .in_30(Out28), .in_31(Out29), .in_32(Out30), .in_33(out_13), .out_34(out_12));
  Register #(.width(32)) register_21 (.D(in_6), .en(L5), .Q(Out5), .clk(in_7), .clr(in_1));
  Register #(.width(32)) register_22 (.D(in_6), .en(L13), .Q(Out13), .clk(in_7), .clr(in_1));
  Register #(.width(32)) register_23 (.D(in_6), .en(L21), .Q(Out21), .clk(in_7), .clr(in_1));
  Register #(.width(32)) register_24 (.D(in_6), .en(L29), .Q(Out29), .clk(in_7), .clr(in_1));
  or or_1 (or_1_out, in_3, in_9);
  Register #(.width(32)) register_25 (.D(in_6), .en(L6), .Q(Out6), .clk(in_7), .clr(in_1));
  Register #(.width(32)) register_26 (.D(in_6), .en(L14), .Q(Out14), .clk(in_7), .clr(in_1));
  Register #(.width(32)) register_27 (.D(in_6), .en(L22), .Q(Out22), .clk(in_7), .clr(in_1));
  Register #(.width(32)) register_28 (.D(in_6), .en(L30), .Q(Out30), .clk(in_7), .clr(in_1));
  Subtractor #(.width(32)) subtractor_1 (.a(out_13), .b(32'h4), .out(subtractor_1_out));  // open: bin, bout
  Adder #(.width(32)) adder_1 (.a(32'h4), .b(out_13), .out(adder_1_out));  // open: cin, cout
  and and_1 (L31, in_8, or_1_out);
  Multiplexer #(.width(32)) multiplexer_3 (
    .in0(subtractor_1_out), .in1(adder_1_out), .out(multiplexer_3_out), .sel(in_9));  // open: en
  or or_2 (or_2_out, L31, in_1);
  Multiplexer #(.width(32)) multiplexer_4 (
    .in0(multiplexer_3_out), .in1({32{1'b1}}), .out(InputSP), .sel(in_1));  // open: en
  Register #(.width(32)) register_29 (.D(in_6), .en(L7), .Q(Out7), .clk(in_7), .clr(in_1));
  Register #(.width(32)) register_30 (.D(in_6), .en(L15), .Q(Out15), .clk(in_7), .clr(in_1));
  Register #(.width(32)) register_31 (.D(in_6), .en(L23), .Q(Out23), .clk(in_7), .clr(in_1));
  Register #(.width(32)) register_32 (.D(InputSP), .en(or_2_out), .Q(out_13), .clk(in_7));  // open: clr

  // Other names for the same wires on the sheet: A[31:0] = out_11; B[31:0] = out_12; clk = in_7; Input[31:0] = in_6;
  //   MemRW = in_8; Out31[31:0] = out_13; outA[4:0] = in_5; outB[4:0] = in_10; pop = in_9; push = in_3; reset = in_1;
  //   sel[4:0] = in_4; write = in_2
endmodule

module multiplexer (
  input  [4:0] in_1,
  input  [31:0] in_2,
  input  [31:0] in_3,
  input  [31:0] in_4,
  input  [31:0] in_5,
  input  [31:0] in_6,
  input  [31:0] in_7,
  input  [31:0] in_8,
  input  [31:0] in_9,
  input  [31:0] in_10,
  input  [31:0] in_11,
  input  [31:0] in_12,
  input  [31:0] in_13,
  input  [31:0] in_14,
  input  [31:0] in_15,
  input  [31:0] in_16,
  input  [31:0] in_17,
  input  [31:0] in_18,
  input  [31:0] in_19,
  input  [31:0] in_20,
  input  [31:0] in_21,
  input  [31:0] in_22,
  input  [31:0] in_23,
  input  [31:0] in_24,
  input  [31:0] in_25,
  input  [31:0] in_26,
  input  [31:0] in_27,
  input  [31:0] in_28,
  input  [31:0] in_29,
  input  [31:0] in_30,
  input  [31:0] in_31,
  input  [31:0] in_32,
  input  [31:0] in_33,
  output [31:0] out_34
);

  wire _0, _1, _2, _3, _4, _5, _6, _7, _8, _9, _10, _11, _12, _13, _14, _15, _16, _17, _18, _19, _20, _21,
       _22, _23, _24, _25, _26, _27, _28, _29, _30, _31;
  wire [31:0] and_1_out, and_2_out, and_3_out, and_4_out, and_5_out, and_6_out, and_7_out, and_8_out,
       and_9_out, and_10_out, and_11_out, and_12_out, and_13_out, and_14_out, and_15_out, and_16_out,
       and_17_out, and_18_out, and_19_out, and_20_out, and_21_out, and_22_out, and_23_out, and_24_out,
       and_25_out, and_26_out, and_27_out, and_28_out, and_29_out, and_30_out, and_31_out, and_32_out,
       bit_extender_1_out, bit_extender_2_out, bit_extender_3_out, bit_extender_4_out, bit_extender_5_out,
       bit_extender_6_out, bit_extender_7_out, bit_extender_8_out, bit_extender_9_out, bit_extender_10_out,
       bit_extender_11_out, bit_extender_12_out, bit_extender_13_out, bit_extender_14_out,
       bit_extender_15_out, bit_extender_16_out, bit_extender_17_out, bit_extender_18_out,
       bit_extender_19_out, bit_extender_20_out, bit_extender_21_out, bit_extender_22_out,
       bit_extender_23_out, bit_extender_24_out, bit_extender_25_out, bit_extender_26_out,
       bit_extender_27_out, bit_extender_28_out, bit_extender_29_out, bit_extender_30_out,
       bit_extender_31_out, bit_extender_32_out;

  Decoder #(.select(5)) decoder_1 (
    .out0(_0), .out1(_1), .out2(_2), .out3(_3), .out4(_4), .out5(_5), .out6(_6), .out7(_7), .out8(_8),
    .out9(_9), .out10(_10), .out11(_11), .out12(_12), .out13(_13), .out14(_14), .out15(_15), .out16(_16),
    .out17(_17), .out18(_18), .out19(_19), .out20(_20), .out21(_21), .out22(_22), .out23(_23), .out24(_24),
    .out25(_25), .out26(_26), .out27(_27), .out28(_28), .out29(_29), .out30(_30), .out31(_31), .sel(in_1));  // open: en
  assign bit_extender_1_out = {{31{_0}}, _0};  // Bit_Extender bit_extender_1
  assign bit_extender_2_out = {{31{_1}}, _1};  // Bit_Extender bit_extender_2
  assign bit_extender_3_out = {{31{_2}}, _2};  // Bit_Extender bit_extender_3
  assign bit_extender_4_out = {{31{_3}}, _3};  // Bit_Extender bit_extender_4
  assign bit_extender_5_out = {{31{_4}}, _4};  // Bit_Extender bit_extender_5
  assign bit_extender_6_out = {{31{_5}}, _5};  // Bit_Extender bit_extender_6
  assign bit_extender_7_out = {{31{_6}}, _6};  // Bit_Extender bit_extender_7
  assign bit_extender_8_out = {{31{_7}}, _7};  // Bit_Extender bit_extender_8
  assign bit_extender_9_out = {{31{_8}}, _8};  // Bit_Extender bit_extender_9
  assign bit_extender_10_out = {{31{_9}}, _9};  // Bit_Extender bit_extender_10
  assign bit_extender_11_out = {{31{_10}}, _10};  // Bit_Extender bit_extender_11
  assign bit_extender_12_out = {{31{_11}}, _11};  // Bit_Extender bit_extender_12
  assign bit_extender_13_out = {{31{_12}}, _12};  // Bit_Extender bit_extender_13
  assign bit_extender_14_out = {{31{_13}}, _13};  // Bit_Extender bit_extender_14
  assign bit_extender_15_out = {{31{_14}}, _14};  // Bit_Extender bit_extender_15
  assign bit_extender_16_out = {{31{_15}}, _15};  // Bit_Extender bit_extender_16
  assign bit_extender_17_out = {{31{_16}}, _16};  // Bit_Extender bit_extender_17
  assign bit_extender_18_out = {{31{_17}}, _17};  // Bit_Extender bit_extender_18
  assign bit_extender_19_out = {{31{_18}}, _18};  // Bit_Extender bit_extender_19
  assign bit_extender_20_out = {{31{_19}}, _19};  // Bit_Extender bit_extender_20
  assign bit_extender_21_out = {{31{_20}}, _20};  // Bit_Extender bit_extender_21
  assign bit_extender_22_out = {{31{_21}}, _21};  // Bit_Extender bit_extender_22
  assign bit_extender_23_out = {{31{_22}}, _22};  // Bit_Extender bit_extender_23
  assign bit_extender_24_out = {{31{_23}}, _23};  // Bit_Extender bit_extender_24
  assign bit_extender_25_out = {{31{_24}}, _24};  // Bit_Extender bit_extender_25
  assign bit_extender_26_out = {{31{_25}}, _25};  // Bit_Extender bit_extender_26
  assign bit_extender_27_out = {{31{_26}}, _26};  // Bit_Extender bit_extender_27
  assign bit_extender_28_out = {{31{_27}}, _27};  // Bit_Extender bit_extender_28
  assign bit_extender_29_out = {{31{_28}}, _28};  // Bit_Extender bit_extender_29
  assign bit_extender_30_out = {{31{_30}}, _30};  // Bit_Extender bit_extender_30
  assign and_1_out = in_2 & bit_extender_1_out;  // AND_Gate and_1, 32 bits wide
  assign and_2_out = in_3 & bit_extender_2_out;  // AND_Gate and_2, 32 bits wide
  assign and_3_out = in_4 & bit_extender_3_out;  // AND_Gate and_3, 32 bits wide
  assign and_4_out = in_5 & bit_extender_4_out;  // AND_Gate and_4, 32 bits wide
  assign and_5_out = in_6 & bit_extender_5_out;  // AND_Gate and_5, 32 bits wide
  assign and_6_out = in_7 & bit_extender_6_out;  // AND_Gate and_6, 32 bits wide
  assign and_7_out = in_8 & bit_extender_7_out;  // AND_Gate and_7, 32 bits wide
  assign and_8_out = in_9 & bit_extender_8_out;  // AND_Gate and_8, 32 bits wide
  assign and_9_out = in_10 & bit_extender_9_out;  // AND_Gate and_9, 32 bits wide
  assign and_10_out = in_11 & bit_extender_10_out;  // AND_Gate and_10, 32 bits wide
  assign and_11_out = in_12 & bit_extender_11_out;  // AND_Gate and_11, 32 bits wide
  assign and_12_out = in_13 & bit_extender_12_out;  // AND_Gate and_12, 32 bits wide
  assign and_13_out = in_14 & bit_extender_13_out;  // AND_Gate and_13, 32 bits wide
  assign and_14_out = in_16 & bit_extender_15_out;  // AND_Gate and_14, 32 bits wide
  assign and_15_out = in_18 & bit_extender_17_out;  // AND_Gate and_15, 32 bits wide
  assign and_16_out = in_20 & bit_extender_19_out;  // AND_Gate and_16, 32 bits wide
  assign bit_extender_31_out = {{31{_29}}, _29};  // Bit_Extender bit_extender_31
  assign bit_extender_32_out = {{31{_31}}, _31};  // Bit_Extender bit_extender_32
  assign and_17_out = in_15 & bit_extender_14_out;  // AND_Gate and_17, 32 bits wide
  assign and_18_out = in_17 & bit_extender_16_out;  // AND_Gate and_18, 32 bits wide
  assign and_19_out = in_19 & bit_extender_18_out;  // AND_Gate and_19, 32 bits wide
  assign and_20_out = in_21 & bit_extender_20_out;  // AND_Gate and_20, 32 bits wide
  assign and_21_out = in_22 & bit_extender_21_out;  // AND_Gate and_21, 32 bits wide
  assign and_22_out = in_23 & bit_extender_22_out;  // AND_Gate and_22, 32 bits wide
  assign and_23_out = in_24 & bit_extender_23_out;  // AND_Gate and_23, 32 bits wide
  assign and_24_out = in_25 & bit_extender_24_out;  // AND_Gate and_24, 32 bits wide
  assign and_25_out = in_26 & bit_extender_25_out;  // AND_Gate and_25, 32 bits wide
  assign and_26_out = in_27 & bit_extender_26_out;  // AND_Gate and_26, 32 bits wide
  assign and_27_out = in_28 & bit_extender_27_out;  // AND_Gate and_27, 32 bits wide
  assign and_28_out = in_29 & bit_extender_28_out;  // AND_Gate and_28, 32 bits wide
  assign and_29_out = in_30 & bit_extender_29_out;  // AND_Gate and_29, 32 bits wide
  assign and_30_out = in_31 & bit_extender_31_out;  // AND_Gate and_30, 32 bits wide
  assign and_31_out = in_32 & bit_extender_30_out;  // AND_Gate and_31, 32 bits wide
  assign and_32_out = in_33 & bit_extender_32_out;  // AND_Gate and_32, 32 bits wide
  assign out_34 = and_1_out | and_2_out | and_3_out | and_4_out | and_5_out | and_6_out | and_7_out | and_8_out | and_9_out | and_10_out | and_11_out | and_12_out | and_13_out | and_17_out | and_14_out | and_18_out | and_15_out | and_19_out | and_16_out | and_20_out | and_21_out | and_22_out | and_23_out | and_24_out | and_25_out | and_26_out | and_27_out | and_28_out | and_29_out | and_30_out | and_31_out | and_32_out;  // OR_Gate or_1, 32 bits wide
endmodule

module instruction_decoder (
  input  [31:0] Instruction,
  output [5:0] out_2,
  output [4:0] Read1,
  output [4:0] Read2,
  output [4:0] Destiny,
  output [5:0] out_6,
  output [15:0] out_7,
  output [25:0] Destiny_2,
  output R,
  output I,
  output J
);

  wire comparator_1_eq, comparator_2_eq, comparator_3_eq;

  Comparator #(.width(6)) comparator_1 (.a(Instruction[7:2]), .b({6{1'b0}}), .eq(comparator_1_eq));  // open: gt, lt
  Comparator #(.width(6)) comparator_2 (.a(Instruction[7:2]), .b({6{1'b1}}), .eq(comparator_2_eq));  // open: gt, lt
  Comparator #(.width(6)) comparator_3 (.a(Instruction[7:2]), .b(6'b111000), .eq(comparator_3_eq));  // open: gt, lt
  Comparator #(.width(6)) comparator_4 (.a(Instruction[7:2]), .b(6'b000010), .eq(J));  // open: gt, lt
  or or_1 (R, comparator_1_eq, comparator_2_eq, comparator_3_eq);
  Multiplexer #(.width(5), .enable("false")) multiplexer_1 (
    .in0(Instruction[12:8]), .in1(Instruction[23:19]), .out(Destiny), .sel(R));
  // Probe on {Instruction[23:16], Instruction[31:24]}
  nor nor_1 (I, R, J);

  assign Destiny_2 = {Instruction[1:0], Instruction[15:8], Instruction[23:16], Instruction[31:24]};
  assign out_2 = Instruction[7:2];
  assign out_6 = Instruction[29:24];
  assign out_7 = {Instruction[23:16], Instruction[31:24]};
  assign Read1 = {Instruction[1:0], Instruction[15:13]};
  assign Read2 = Instruction[12:8];

  // Other names for the same wires on the sheet: Const[15:0] = {Instruction[23:16], Instruction[31:24]};
  //   FUNC_CODE[5:0] = Instruction[29:24]; X[4:0] = {Instruction[18:16], Instruction[31:30]};
  //   RD[4:0] = Instruction[23:19]; RT[4:0] = Instruction[12:8]; RS[4:0] = {Instruction[1:0], Instruction[15:13]};
  //   OPCODE[5:0] = Instruction[7:2]
endmodule
